# Fritzing sketch Skecth (saved by Fritzing 0.9.3b)
breadboards: 1

parts:
  PIR1 = PIR sensor
  Raspberry_Pi_1 = Raspberry Pi 3 [part_number=RPI-3-V1.2]
  LED1 = RGB LED (com. anode, rbg) [package="5 mm [THT]"]
  LED2 = RGB LED (com. anode, rbg) [package="5 mm [THT]"]
  CAMERA1 = TTL Serial JPEG Camera
  USBTTL2 = USB A Plug

nets:
  VDD: PIR1.VDD, Raspberry_Pi_1.5V
  N1: PIR1.SIG, Raspberry_Pi_1.GIPO18, Raspberry_Pi_1.GIPO15
  GND: PIR1.GND, Raspberry_Pi_1.GIPO4, Raspberry_Pi_1.GND, LED1.green_cathode, LED2.green_cathode
  N2: Raspberry_Pi_1.GIPO17, LED1.common_anode
  N3: Raspberry_Pi_1.GIPO27, LED2.common_anode
  N4: CAMERA1.GND, USBTTL2.usb

notes:
  USB Cable connection

custom parts:
  TTL Serial JPEG Camera: TTL Serial JPEG Camera with NTSC Out
